# Fritzing sketch Final Wiring (saved by Fritzing 1.0.2b)
breadboards: 1

parts:
  Part1 = Arduino Nano (Rev3.0) (ICSP)
  Part2 = MQ-3 breakout

nets:
  N1: Part1.D5, Part2.DO
  GND: Part1.GND, Part2.GND
  5V: Part1.5V, Part2.VCC
  N2: Part1.A6, Part2.AO

custom parts:
  MQ-3 breakout: Alcohol sensor is capable of detecting alcohol (ethanol) particles on itself and gives the information in digital form back to us to manipulate with it. SKU:101251 • Voltage: 5V DC • Power: max 750mW • Measurement range: 0.04-4mg/L
